// Digital circuit main_simulation.dig as structural Verilog
module main_simulation (
  input  [3:0] bin_in,
  input  reset
);

  wire [6:0] u_hex_decoder_seg_ones, u_hex_decoder_seg_tens;

  hex_decoder #(.applicationType("IVERILOG"), .CodeFile("C:\\Users\\jcnru\\Desktop\\sidequest\\verilog\\hdl_project\\verilog_design_code\\hex_decoder.v")) u_hex_decoder (
    .bin_in(bin_in), .reset(reset), .seg_tens(u_hex_decoder_seg_tens), .seg_ones(u_hex_decoder_seg_ones));
  Seven_Seg seven_seg_1 (
    .a(u_hex_decoder_seg_tens[0]), .b(u_hex_decoder_seg_tens[1]), .c(u_hex_decoder_seg_tens[2]),
    .d(u_hex_decoder_seg_tens[3]), .e(u_hex_decoder_seg_tens[4]), .f(u_hex_decoder_seg_tens[5]),
    .g(u_hex_decoder_seg_tens[6]), .dp(1'b0));
  Seven_Seg seven_seg_2 (
    .a(u_hex_decoder_seg_ones[0]), .b(u_hex_decoder_seg_ones[1]), .c(u_hex_decoder_seg_ones[2]),
    .d(u_hex_decoder_seg_ones[3]), .e(u_hex_decoder_seg_ones[4]), .f(u_hex_decoder_seg_ones[5]),
    .g(u_hex_decoder_seg_ones[6]), .dp(1'b0));
endmodule
